// Logisim project CPU.circ as structural Verilog: 2 circuits, main circuit main
module main (
);

  ALU_8bit alu_8bit_1 ();  // open: A0, A1, A2, A3, A4, A5, A6, A7, B0, B1, B2, B3, B4, B5, B6, B7, O0, O1, O2, O3, C0, C1, C2, C3, C4, C5, C6, C7
endmodule

module ALU_8bit (
  input  O0,
  input  O1,
  input  A0,
  input  O2,
  input  A1,
  input  O3,
  input  A2,
  input  A3,
  input  A4,
  input  A5,
  input  A6,
  input  A7,
  input  B0,
  input  B1,
  input  B2,
  input  B3,
  input  B4,
  input  B5,
  input  B6,
  input  B7,
  output C0,
  output C1,
  output C2,
  output C3,
  output C4,
  output C5,
  output C6,
  output C7
);

  wire [7:0] adder_1_out, and_1_out, divider_1_out, multiplier_1_out, nand_1_out, nor_1_out, not_1_out,
       or_1_out, subtractor_1_out, xor_1_out;

  assign and_1_out = {A7, A6, A5, A4, A3, A2, A1, A0} & {B7, B6, B5, B4, B3, B2, B1, B0};  // AND_Gate and_1, 8 bits wide
  assign or_1_out = {A7, A6, A5, A4, A3, A2, A1, A0} | {B7, B6, B5, B4, B3, B2, B1, B0};  // OR_Gate or_1, 8 bits wide
  assign xor_1_out = {A7, A6, A5, A4, A3, A2, A1, A0} ^ {B7, B6, B5, B4, B3, B2, B1, B0};  // XOR_Gate xor_1, 8 bits wide
  assign nand_1_out = ~({A7, A6, A5, A4, A3, A2, A1, A0} & {B7, B6, B5, B4, B3, B2, B1, B0});  // NAND_Gate nand_1, 8 bits wide
  assign nor_1_out = ~({A7, A6, A5, A4, A3, A2, A1, A0} | {B7, B6, B5, B4, B3, B2, B1, B0});  // NOR_Gate nor_1, 8 bits wide
  Adder adder_1 (
    .a({A7, A6, A5, A4, A3, A2, A1, A0}), .b({B7, B6, B5, B4, B3, B2, B1, B0}), .out(adder_1_out));  // open: cin, cout
  Subtractor subtractor_1 (
    .a({A7, A6, A5, A4, A3, A2, A1, A0}), .b({B7, B6, B5, B4, B3, B2, B1, B0}), .out(subtractor_1_out));  // open: bin, bout
  Multiplier multiplier_1 (
    .a({A7, A6, A5, A4, A3, A2, A1, A0}), .b({B7, B6, B5, B4, B3, B2, B1, B0}), .out(multiplier_1_out));  // open: cin, cout
  Divider divider_1 (
    .a({A7, A6, A5, A4, A3, A2, A1, A0}), .b({B7, B6, B5, B4, B3, B2, B1, B0}), .out(divider_1_out));  // open: upper, rem
  assign not_1_out = ~{A7, A6, A5, A4, A3, A2, A1, A0};  // NOT_Gate not_1, 8 bits wide
  Multiplexer #(.select(4), .width(8)) multiplexer_1 (
    .in0({A7, A6, A5, A4, A3, A2, A1, A0}), .in1(not_1_out), .in2(and_1_out), .in3(or_1_out),
    .in4(xor_1_out), .in5(nand_1_out), .in6(nor_1_out), .in7({8{1'b1}}), .in8({8{1'b0}}), .in9(adder_1_out),
    .in10(subtractor_1_out), .in11(multiplier_1_out), .in12(divider_1_out),
    .out({C7, C6, C5, C4, C3, C2, C1, C0}), .sel({O3, O2, O1, O0}));  // open: in13, in14, in15, en
endmodule
